# Fritzing sketch electronics (saved by Fritzing 1.0.5)

parts:
  Bauteil1 = Adafruit TCA9548A
  INA1 = INA219 DC Current Sensor Breakout  # not connected
  INA2 = INA219 DC Current Sensor Breakout  # not connected
  INA3 = INA219 DC Current Sensor Breakout  # not connected
  INA4 = INA219 DC Current Sensor Breakout  # not connected
  INA5 = INA219 DC Current Sensor Breakout  # not connected
  INA6 = INA219 DC Current Sensor Breakout  # not connected
  MCU1 = Raspberry Pi Zero
  F1 = Fan - Ventilador [package=THT]  # not connected
  o1 = Module display OLED I2C 128x64 SSD1306 [package=THT]

nets:
  N1: Bauteil1.INPUTSDA, MCU1.pin_3
  N2: Bauteil1.INPUTSCL, MCU1.pin_5
  N3: MCU1.pin_2, MCU1.pin_4
  N4: MCU1.pin_6, MCU1.pin_9, MCU1.pin_20
  N5: MCU1.pin_27, o1.SDA
  N6: MCU1.pin_28, o1.SCL

custom parts:
  Adafruit TCA9548A: You just found the perfect I2C sensor, and you want to wire up two or three or more of them to your Arduino when you realize "Uh oh, this chip has a fixed I2C address, and from what I know about I2C, you cannot have two devices with the same address on the same SDA/SCL pins!" Are you out of luck? You would be, if you didn't have this ultra-cool TCA9548A 1-to-8 I2C multiplexer! Finally, a way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
  INA219 DC Current Sensor Breakout: INA DC Current Sensor Breakout
  Fan - Ventilador: Ventilador de 2 pines, se encuentra comunmente en computadoras de escritorio
  Module display OLED I2C 128x64 SSD1306: Ecran OLED I2C SSD163 de 128x64 avec connexion I2C
