# Fritzing sketch schaltplan (saved by Fritzing 1.0.6)

parts:
  RS1 = RS232 Shield
  Mod1 = Raspberry Pi 4B
  MCU1 = Raspberry Pi Zero  # not connected
  Grove1 = Grove OLED 128x96  # not connected
  X1 = DB9 Connector [package=db9]  # not connected
  J1 = Camdenboss CTB0158-4 [part_number=CTB0158-4 package=THT]  # not connected

nets:
  N1: RS1.RXD, Mod1.GPIO14
  N2: RS1.TXD, Mod1.GPIO15
  GND: RS1.GND, Mod1.GND
  VCC: RS1.VCC, Mod1.5V

notes:
  RXD - TX am Automaten
  GND
  TXD - RX am Automaten
  Steckerleiste am Automaten
  Master receive - automat tx
  Master transmit - automat rx

custom parts:
  RS232 Shield: RS232 connector, 4-pin, right-angle female. Designed by Dr Kristofer Chan, King's College London / remote-research.org. Licensed under Creative Commons Attribution-ShareAlike 4.0
